// Logisim project Assignment-2 Circuit.circ as structural Verilog: 1 circuit, main circuit main
module main (
  input  C,
  input  in_2,
  input  [1:0] INPUT,
  input  ENABLER,
  output SUM,
  output CARRY
);

  wire not_1_out;

  not not_1 (not_1_out, C);
  Multiplexer #(.select(2)) multiplexer_1 (
    .in0(C), .in1(not_1_out), .in2(not_1_out), .in3(C), .out(SUM), .sel(INPUT), .en(ENABLER));
  Multiplexer #(.select(2)) multiplexer_2 (
    .in0(in_2), .in1(C), .in2(C), .in3(1'b1), .out(CARRY), .sel(INPUT), .en(ENABLER));
endmodule
