// Logisim project Lab2 no.2.circ as structural Verilog: 1 circuit, main circuit main
module main (
  input  A,
  input  B,
  input  A_2,
  input  B_2,
  output out_5,
  output out_6
);

  wire nand_1_out, nand_2_out, nand_3_out, nand_4_out, nand_5_out, nand_6_out, nand_7_out;

  nand nand_1 (nand_1_out, A, B);
  nand nand_2 (nand_2_out, A_2, A_2);
  nand nand_3 (nand_3_out, B_2, B_2);
  nand nand_4 (nand_4_out, A, nand_1_out);
  nand nand_5 (nand_5_out, nand_1_out, B);
  nand nand_6 (nand_6_out, A_2, B_2);
  nand nand_7 (nand_7_out, nand_2_out, nand_3_out);
  nand nand_8 (out_5, nand_4_out, nand_5_out);
  nand nand_9 (out_6, nand_6_out, nand_7_out);

  // Notes on the sheet:
  //   XOR using NAND Gate
  //   XNOR using NAND Gate
endmodule
